# Fritzing sketch Lantern (saved by Fritzing 0.9.3b)
breadboards: 1

parts:
  Piezo_Element = Piezo Speaker
  1_Mohm = Resistor [tolerance=±5% resistance=1M package=THT]
  MCP602_Dual_Op_Amps_1 = Dual Op-Amp [package=dip08]
  R1 = Resistor [tolerance=±5% resistance=330k package=THT]
  R2 = Resistor [tolerance=±5% resistance=10k package=THT]
  D1 = Rectifier Diode [part_number=1N4001 package="300 mil [THT]"]
  C1 = Tantalum Capacitor [capacitance=1μF package="100 mil [THT, tantalum]"]
  R3 = Resistor [tolerance=±5% resistance=470k package=THT]
  MCP602_Dual_Op_Amps_2 = Dual Op-Amp [package=dip08]
  R4 = Resistor [tolerance=±5% resistance=100 package=THT]
  R5 = Resistor [tolerance=±5% resistance=560 package=THT]
  R6 = Resistor [tolerance=±5% resistance=100 package=THT]
  R7 = Resistor [tolerance=±5% resistance=18 package=THT]
  Part1 = 24 NeoPixel Ring [part_number=1586]
  REG1 = LD33 Low-Dropout Voltage Regulator
  Part2 = Arduino Uno (Rev3) - ICSP
  1000_uF_cap = Capacitor Polarized [package=cpol-radial-1000uf-63v]
  Pot = Rotary Potentiometer (Large) [maximum_resistance=100kΩ package=THT]
  U1 = ESP8266 WiFi Module [part_number=ESP8266]
  STATUS_LED = LEDs [package=led10mm]
  R8 = Resistor [tolerance=±2% resistance=250 package="2010 [SMD]"]
  U2 = ATmega 328P [package=dip]  # not connected

nets:
  GND: Piezo_Element.pin1, 1_Mohm.Pin_0, MCP602_Dual_Op_Amps_1.A_V+, R2.Pin_0, C1.-, R3.Pin_1, MCP602_Dual_Op_Amps_2.A_V+, R7.Pin_1, Part1.GND, REG1.GND, Part2.GND, 1000_uF_cap.-, Pot.leg1, U1.GND, R8.Pin_1
  NonInv Amp (33x): Piezo_Element.pin2, 1_Mohm.Pin_1, MCP602_Dual_Op_Amps_1.A_+IN
  N1: MCP602_Dual_Op_Amps_1.A_OUT, R1.Pin_0, D1.anode
  N2: MCP602_Dual_Op_Amps_1.A_-IN, R1.Pin_1, R2.Pin_1
  5V: MCP602_Dual_Op_Amps_1.A_V-, MCP602_Dual_Op_Amps_2.A_V-, R6.Pin_0, Part1.VDD, REG1.Vin, Part2.VIN, 1000_uF_cap.+, Pot.leg2
  Percussive Envelope Detector: MCP602_Dual_Op_Amps_1.B_+IN, D1.cathode, C1.+, R3.Pin_0
  Buffer: MCP602_Dual_Op_Amps_1.B_-IN, MCP602_Dual_Op_Amps_1.B_OUT, R4.Pin_0
  SIG Out: MCP602_Dual_Op_Amps_2.A_OUT, R5.Pin_1, Part2.D2
  ~0.8 V Ref: MCP602_Dual_Op_Amps_2.A_-IN, R6.Pin_1, R7.Pin_0
  Schmitt Trigger Comparator: MCP602_Dual_Op_Amps_2.A_+IN, R4.Pin_1, R5.Pin_0
  N3: Part1.IN, Part2.D8
  N4: REG1.Vout, U1.VCC
  N5: Part2.A1, Pot.wiper
  N6: Part2.D3_PWM, U1.GPIO_2
  N7: Part2.D6_PWM, STATUS_LED.A
  N8: STATUS_LED.C, R8.Pin_0

custom parts:
  24 NeoPixel Ring: 24 ultra bright smart LED NeoPixels are arranged in a circle with 2.6" (66mm) outer diameter. The rings are 'chainable' - connect the output pin of one to the input pin of another. Use only one microcontroller pin to control as many as you can chain together! Each LED is addressable as the driver chip is inside the LED. Each one has ~18mA constant current drive so the color will be very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
  ATmega 328P: Atmel ATmega 328P-PU Microcontroller
